// Logisim project Lab1.circ as structural Verilog: 14 circuits, main circuit main
module main (
  input  X
);

  wire C1, C2, C3, clock_1_out, Reset_out, siete_segmentos_1_a, siete_segmentos_1_b, siete_segmentos_1_c,
       siete_segmentos_1_d, siete_segmentos_1_e, siete_segmentos_1_f, siete_segmentos_1_g,
       siete_segmentos_2_a, siete_segmentos_2_b, siete_segmentos_2_c, siete_segmentos_2_d,
       siete_segmentos_2_e, siete_segmentos_2_f, siete_segmentos_2_g, siete_segmentos_3_a,
       siete_segmentos_3_b, siete_segmentos_3_c, siete_segmentos_3_d, siete_segmentos_3_e,
       siete_segmentos_3_f, siete_segmentos_3_g, siete_segmentos_4_a, siete_segmentos_4_b,
       siete_segmentos_4_c, siete_segmentos_4_d, siete_segmentos_4_e, siete_segmentos_4_f,
       siete_segmentos_4_g, siete_segmentos_5_a, siete_segmentos_5_b, siete_segmentos_5_c,
       siete_segmentos_5_d, siete_segmentos_5_e, siete_segmentos_5_f, siete_segmentos_5_g,
       siete_segmentos_6_a, siete_segmentos_6_b, siete_segmentos_6_c, siete_segmentos_6_d,
       siete_segmentos_6_e, siete_segmentos_6_f, siete_segmentos_6_g, siete_segmentos_7_a,
       siete_segmentos_7_b, siete_segmentos_7_c, siete_segmentos_7_d, siete_segmentos_7_e,
       siete_segmentos_7_f, siete_segmentos_7_g, siete_segmentos_8_a, siete_segmentos_8_b,
       siete_segmentos_8_c, siete_segmentos_8_d, siete_segmentos_8_e, siete_segmentos_8_f,
       siete_segmentos_8_g, siete_segmentos_9_a, siete_segmentos_9_b, siete_segmentos_9_c,
       siete_segmentos_9_d, siete_segmentos_9_e, siete_segmentos_9_f, siete_segmentos_9_g,
       siete_segmentos_10_a, siete_segmentos_10_b, siete_segmentos_10_c, siete_segmentos_10_d,
       siete_segmentos_10_e, siete_segmentos_10_f, siete_segmentos_10_g, siete_segmentos_11_a,
       siete_segmentos_11_b, siete_segmentos_11_c, siete_segmentos_11_d, siete_segmentos_11_e,
       siete_segmentos_11_f, siete_segmentos_11_g;
  wire [3:0] bcd_1_d, bcd_1_u, bcd_2_c, bcd_2_d, bcd_2_u, bcd_3_c, bcd_3_d, bcd_3_u, bcd_4_c, bcd_4_d,
       bcd_4_u, tressecuenciasunion_1_sn;
  wire [7:0] contadorjk_1_q0, contadorjk_2_q0, contadorjk_3_q0;
  wire [7:4] undriven;

  Clock clock_1 (.out(clock_1_out));
  Button Reset (.out(Reset_out));
  // Probe on tressecuenciasunion_1_sn
  contadorJK contadorjk_1 (
    .X(C3), .CLK(clock_1_out), .Reset(Reset_out), .Q0(contadorjk_1_q0[0]), .Q1(contadorjk_1_q0[1]),
    .Q2(contadorjk_1_q0[2]), .Q3(contadorjk_1_q0[3]), .Q4(contadorjk_1_q0[4]), .Q5(contadorjk_1_q0[5]),
    .Q6(contadorjk_1_q0[6]), .Q7(contadorjk_1_q0[7]));
  tresSecuenciasUnion tressecuenciasunion_1 (
    .X(X), .CLK(clock_1_out), .Reset(Reset_out), .Sn(tressecuenciasunion_1_sn), .Z1(C1), .Z2(C2), .Z3(C3));
  contadorJK contadorjk_2 (
    .X(C1), .CLK(clock_1_out), .Reset(Reset_out), .Q0(contadorjk_2_q0[0]), .Q1(contadorjk_2_q0[1]),
    .Q2(contadorjk_2_q0[2]), .Q3(contadorjk_2_q0[3]), .Q4(contadorjk_2_q0[4]), .Q5(contadorjk_2_q0[5]),
    .Q6(contadorjk_2_q0[6]), .Q7(contadorjk_2_q0[7]));
  contadorJK contadorjk_3 (
    .X(C2), .CLK(clock_1_out), .Reset(Reset_out), .Q0(contadorjk_3_q0[0]), .Q1(contadorjk_3_q0[1]),
    .Q2(contadorjk_3_q0[2]), .Q3(contadorjk_3_q0[3]), .Q4(contadorjk_3_q0[4]), .Q5(contadorjk_3_q0[5]),
    .Q6(contadorjk_3_q0[6]), .Q7(contadorjk_3_q0[7]));
  BCD bcd_1 (.Count({undriven, tressecuenciasunion_1_sn}), .u(bcd_1_u), .d(bcd_1_d));  // open: c
  BCD bcd_2 (.Count(contadorjk_2_q0), .c(bcd_2_c), .u(bcd_2_u), .d(bcd_2_d));
  BCD bcd_3 (.Count(contadorjk_3_q0), .c(bcd_3_c), .u(bcd_3_u), .d(bcd_3_d));
  BCD bcd_4 (.Count(contadorjk_1_q0), .c(bcd_4_c), .u(bcd_4_u), .d(bcd_4_d));
  siete_segmentos siete_segmentos_1 (
    .W(bcd_1_d[3]), .X(bcd_1_d[2]), .Y(bcd_1_d[1]), .Z(bcd_1_d[0]), .A(siete_segmentos_1_a),
    .B(siete_segmentos_1_b), .C(siete_segmentos_1_c), .D(siete_segmentos_1_d), .E(siete_segmentos_1_e),
    .F(siete_segmentos_1_f), .G(siete_segmentos_1_g));
  siete_segmentos siete_segmentos_2 (
    .W(bcd_2_c[3]), .X(bcd_2_c[2]), .Y(bcd_2_c[1]), .Z(bcd_2_c[0]), .A(siete_segmentos_2_a),
    .B(siete_segmentos_2_b), .C(siete_segmentos_2_c), .D(siete_segmentos_2_d), .E(siete_segmentos_2_e),
    .F(siete_segmentos_2_f), .G(siete_segmentos_2_g));
  siete_segmentos siete_segmentos_3 (
    .W(bcd_3_c[3]), .X(bcd_3_c[2]), .Y(bcd_3_c[1]), .Z(bcd_3_c[0]), .A(siete_segmentos_3_a),
    .B(siete_segmentos_3_b), .C(siete_segmentos_3_c), .D(siete_segmentos_3_d), .E(siete_segmentos_3_e),
    .F(siete_segmentos_3_f), .G(siete_segmentos_3_g));
  siete_segmentos siete_segmentos_4 (
    .W(bcd_4_c[3]), .X(bcd_4_c[2]), .Y(bcd_4_c[1]), .Z(bcd_4_c[0]), .A(siete_segmentos_4_a),
    .B(siete_segmentos_4_b), .C(siete_segmentos_4_c), .D(siete_segmentos_4_d), .E(siete_segmentos_4_e),
    .F(siete_segmentos_4_f), .G(siete_segmentos_4_g));
  _7_Segment_Display u_7_segment_display_1 (
    .g(siete_segmentos_1_g), .f(siete_segmentos_1_f), .a(siete_segmentos_1_a), .b(siete_segmentos_1_b),
    .e(siete_segmentos_1_e), .d(siete_segmentos_1_d), .c(siete_segmentos_1_c));  // open: dp
  _7_Segment_Display u_7_segment_display_2 (
    .g(siete_segmentos_2_g), .f(siete_segmentos_2_f), .a(siete_segmentos_2_a), .b(siete_segmentos_2_b),
    .e(siete_segmentos_2_e), .d(siete_segmentos_2_d), .c(siete_segmentos_2_c));  // open: dp
  _7_Segment_Display u_7_segment_display_3 (
    .g(siete_segmentos_3_g), .f(siete_segmentos_3_f), .a(siete_segmentos_3_a), .b(siete_segmentos_3_b),
    .e(siete_segmentos_3_e), .d(siete_segmentos_3_d), .c(siete_segmentos_3_c));  // open: dp
  _7_Segment_Display u_7_segment_display_4 (
    .g(siete_segmentos_4_g), .f(siete_segmentos_4_f), .a(siete_segmentos_4_a), .b(siete_segmentos_4_b),
    .e(siete_segmentos_4_e), .d(siete_segmentos_4_d), .c(siete_segmentos_4_c));  // open: dp
  siete_segmentos siete_segmentos_5 (
    .W(bcd_1_u[3]), .X(bcd_1_u[2]), .Y(bcd_1_u[1]), .Z(bcd_1_u[0]), .A(siete_segmentos_5_a),
    .B(siete_segmentos_5_b), .C(siete_segmentos_5_c), .D(siete_segmentos_5_d), .E(siete_segmentos_5_e),
    .F(siete_segmentos_5_f), .G(siete_segmentos_5_g));
  siete_segmentos siete_segmentos_6 (
    .W(bcd_2_d[3]), .X(bcd_2_d[2]), .Y(bcd_2_d[1]), .Z(bcd_2_d[0]), .A(siete_segmentos_6_a),
    .B(siete_segmentos_6_b), .C(siete_segmentos_6_c), .D(siete_segmentos_6_d), .E(siete_segmentos_6_e),
    .F(siete_segmentos_6_f), .G(siete_segmentos_6_g));
  siete_segmentos siete_segmentos_7 (
    .W(bcd_3_d[3]), .X(bcd_3_d[2]), .Y(bcd_3_d[1]), .Z(bcd_3_d[0]), .A(siete_segmentos_7_a),
    .B(siete_segmentos_7_b), .C(siete_segmentos_7_c), .D(siete_segmentos_7_d), .E(siete_segmentos_7_e),
    .F(siete_segmentos_7_f), .G(siete_segmentos_7_g));
  siete_segmentos siete_segmentos_8 (
    .W(bcd_4_d[3]), .X(bcd_4_d[2]), .Y(bcd_4_d[1]), .Z(bcd_4_d[0]), .A(siete_segmentos_8_a),
    .B(siete_segmentos_8_b), .C(siete_segmentos_8_c), .D(siete_segmentos_8_d), .E(siete_segmentos_8_e),
    .F(siete_segmentos_8_f), .G(siete_segmentos_8_g));
  _7_Segment_Display u_7_segment_display_5 (
    .g(siete_segmentos_5_g), .f(siete_segmentos_5_f), .a(siete_segmentos_5_a), .b(siete_segmentos_5_b),
    .e(siete_segmentos_5_e), .d(siete_segmentos_5_d), .c(siete_segmentos_5_c));  // open: dp
  _7_Segment_Display u_7_segment_display_6 (
    .g(siete_segmentos_6_g), .f(siete_segmentos_6_f), .a(siete_segmentos_6_a), .b(siete_segmentos_6_b),
    .e(siete_segmentos_6_e), .d(siete_segmentos_6_d), .c(siete_segmentos_6_c));  // open: dp
  _7_Segment_Display u_7_segment_display_7 (
    .g(siete_segmentos_7_g), .f(siete_segmentos_7_f), .a(siete_segmentos_7_a), .b(siete_segmentos_7_b),
    .e(siete_segmentos_7_e), .d(siete_segmentos_7_d), .c(siete_segmentos_7_c));  // open: dp
  _7_Segment_Display u_7_segment_display_8 (
    .g(siete_segmentos_8_g), .f(siete_segmentos_8_f), .a(siete_segmentos_8_a), .b(siete_segmentos_8_b),
    .e(siete_segmentos_8_e), .d(siete_segmentos_8_d), .c(siete_segmentos_8_c));  // open: dp
  siete_segmentos siete_segmentos_9 (
    .W(bcd_3_u[3]), .X(bcd_3_u[2]), .Y(bcd_3_u[1]), .Z(bcd_3_u[0]), .A(siete_segmentos_9_a),
    .B(siete_segmentos_9_b), .C(siete_segmentos_9_c), .D(siete_segmentos_9_d), .E(siete_segmentos_9_e),
    .F(siete_segmentos_9_f), .G(siete_segmentos_9_g));
  siete_segmentos siete_segmentos_10 (
    .W(bcd_4_u[3]), .X(bcd_4_u[2]), .Y(bcd_4_u[1]), .Z(bcd_4_u[0]), .A(siete_segmentos_10_a),
    .B(siete_segmentos_10_b), .C(siete_segmentos_10_c), .D(siete_segmentos_10_d), .E(siete_segmentos_10_e),
    .F(siete_segmentos_10_f), .G(siete_segmentos_10_g));
  LED led_1 (.in(C1));
  LED led_2 (.in(C2));
  LED led_3 (.in(C3));
  siete_segmentos siete_segmentos_11 (
    .W(bcd_2_u[3]), .X(bcd_2_u[2]), .Y(bcd_2_u[1]), .Z(bcd_2_u[0]), .A(siete_segmentos_11_a),
    .B(siete_segmentos_11_b), .C(siete_segmentos_11_c), .D(siete_segmentos_11_d), .E(siete_segmentos_11_e),
    .F(siete_segmentos_11_f), .G(siete_segmentos_11_g));
  _7_Segment_Display u_7_segment_display_9 (
    .g(siete_segmentos_9_g), .f(siete_segmentos_9_f), .a(siete_segmentos_9_a), .b(siete_segmentos_9_b),
    .e(siete_segmentos_9_e), .d(siete_segmentos_9_d), .c(siete_segmentos_9_c));  // open: dp
  _7_Segment_Display u_7_segment_display_10 (
    .g(siete_segmentos_10_g), .f(siete_segmentos_10_f), .a(siete_segmentos_10_a), .b(siete_segmentos_10_b),
    .e(siete_segmentos_10_e), .d(siete_segmentos_10_d), .c(siete_segmentos_10_c));  // open: dp
  _7_Segment_Display u_7_segment_display_11 (
    .g(siete_segmentos_11_g), .f(siete_segmentos_11_f), .a(siete_segmentos_11_a), .b(siete_segmentos_11_b),
    .e(siete_segmentos_11_e), .d(siete_segmentos_11_d), .c(siete_segmentos_11_c));  // open: dp
endmodule

module BCD (
  input  [7:0] Count,
  output [3:0] c,
  output [3:0] u,
  output [3:0] d
);

  wire [7:0] divider_1_out;
  wire [7:4] divider_1_rem, divider_2_out, divider_2_rem;

  Divider divider_1 (.a(Count), .b(8'ha), .out(divider_1_out), .rem({divider_1_rem, u}));  // open: upper
  // Probe on divider_1_out
  // Probe on {divider_1_rem, u}
  Divider divider_2 (.a(divider_1_out), .b(8'ha), .out({divider_2_out, c}), .rem({divider_2_rem, d}));  // open: upper
  // Probe on {divider_2_rem, d}
  // Probe on {divider_2_out, c}

  // Other names for the same wires on the sheet: Unidades[3:0] = u; Decenas[3:0] = d; Centenas[3:0] = c

  // Notes on the sheet:
  //   Unidades
endmodule

module siete_segmentos (
  input  W,
  input  X,
  input  Y,
  input  Z,
  output A,
  output B,
  output C,
  output D,
  output E,
  output F,
  output G
);

  wire and_1_out, and_2_out, and_3_out, and_4_out, and_5_out, and_6_out, and_7_out, and_8_out, and_9_out,
       and_10_out, and_11_out, and_12_out, and_13_out, and_14_out, and_15_out, and_16_out, not_1_out,
       not_2_out, not_3_out, or_2_out, or_3_out, or_4_out, or_5_out, or_7_out, or_8_out, or_9_out, or_11_out,
       or_12_out, or_13_out;

  not not_1 (not_1_out, X);
  not not_2 (not_2_out, Y);
  not not_3 (not_3_out, Z);
  and and_1 (and_1_out, not_1_out, not_3_out);
  and and_2 (and_2_out, X, Z);
  and and_3 (and_3_out, Y, Z);
  and and_4 (and_4_out, not_2_out, not_3_out);
  or or_1 (C, X, not_2_out, Z);
  and and_5 (and_5_out, not_1_out, not_3_out);
  and and_6 (and_6_out, not_1_out, Y);
  and and_7 (and_7_out, X, not_2_out, Z);
  and and_8 (and_8_out, Y, not_3_out);
  and and_9 (and_9_out, not_1_out, not_3_out);
  and and_10 (and_10_out, Y, not_3_out);
  and and_11 (and_11_out, not_2_out, not_3_out);
  and and_12 (and_12_out, X, not_3_out);
  and and_13 (and_13_out, X, not_2_out);
  and and_14 (and_14_out, not_1_out, Y);
  and and_15 (and_15_out, X, not_2_out);
  and and_16 (and_16_out, Y, not_3_out);
  or or_2 (or_2_out, Y, and_1_out);
  or or_3 (or_3_out, and_3_out, and_4_out);
  or or_4 (or_4_out, and_5_out, and_6_out);
  or or_5 (or_5_out, and_7_out, and_8_out);
  or or_6 (E, and_9_out, and_10_out);
  or or_7 (or_7_out, and_11_out, and_12_out);
  or or_8 (or_8_out, and_14_out, and_15_out);
  or or_9 (or_9_out, or_2_out, and_2_out);
  or or_10 (B, not_1_out, or_3_out);
  or or_11 (or_11_out, or_4_out, or_5_out);
  or or_12 (or_12_out, or_7_out, and_13_out);
  or or_13 (or_13_out, or_8_out, and_16_out);
  or or_14 (A, W, or_9_out);
  or or_15 (D, W, or_11_out);
  or or_16 (F, W, or_12_out);
  or or_17 (G, W, or_13_out);
endmodule

module Led_7_seg (
  input  [7:0] in_1
);

  wire siete_segmentos_1_a, siete_segmentos_1_b, siete_segmentos_1_c, siete_segmentos_1_d,
       siete_segmentos_1_e, siete_segmentos_1_f, siete_segmentos_1_g, siete_segmentos_2_a,
       siete_segmentos_2_b, siete_segmentos_2_c, siete_segmentos_2_d, siete_segmentos_2_e,
       siete_segmentos_2_f, siete_segmentos_2_g, siete_segmentos_3_a, siete_segmentos_3_b,
       siete_segmentos_3_c, siete_segmentos_3_d, siete_segmentos_3_e, siete_segmentos_3_f,
       siete_segmentos_3_g;
  wire [3:0] bcd_1_c, bcd_1_d, bcd_1_u;

  BCD bcd_1 (.Count(in_1), .c(bcd_1_c), .u(bcd_1_u), .d(bcd_1_d));
  siete_segmentos siete_segmentos_1 (
    .W(bcd_1_c[3]), .X(bcd_1_c[2]), .Y(bcd_1_c[1]), .Z(bcd_1_c[0]), .A(siete_segmentos_1_a),
    .B(siete_segmentos_1_b), .C(siete_segmentos_1_c), .D(siete_segmentos_1_d), .E(siete_segmentos_1_e),
    .F(siete_segmentos_1_f), .G(siete_segmentos_1_g));
  siete_segmentos siete_segmentos_2 (
    .W(bcd_1_u[3]), .X(bcd_1_u[2]), .Y(bcd_1_u[1]), .Z(bcd_1_u[0]), .A(siete_segmentos_2_a),
    .B(siete_segmentos_2_b), .C(siete_segmentos_2_c), .D(siete_segmentos_2_d), .E(siete_segmentos_2_e),
    .F(siete_segmentos_2_f), .G(siete_segmentos_2_g));
  siete_segmentos siete_segmentos_3 (
    .W(bcd_1_d[3]), .X(bcd_1_d[2]), .Y(bcd_1_d[1]), .Z(bcd_1_d[0]), .A(siete_segmentos_3_a),
    .B(siete_segmentos_3_b), .C(siete_segmentos_3_c), .D(siete_segmentos_3_d), .E(siete_segmentos_3_e),
    .F(siete_segmentos_3_f), .G(siete_segmentos_3_g));
  _7_Segment_Display u_7_segment_display_1 (
    .g(siete_segmentos_1_g), .f(siete_segmentos_1_f), .a(siete_segmentos_1_a), .b(siete_segmentos_1_b),
    .e(siete_segmentos_1_e), .d(siete_segmentos_1_d), .c(siete_segmentos_1_c));  // open: dp
  _7_Segment_Display u_7_segment_display_2 (
    .g(siete_segmentos_3_g), .f(siete_segmentos_3_f), .a(siete_segmentos_3_a), .b(siete_segmentos_3_b),
    .e(siete_segmentos_3_e), .d(siete_segmentos_3_d), .c(siete_segmentos_3_c));  // open: dp
  _7_Segment_Display u_7_segment_display_3 (
    .g(siete_segmentos_2_g), .f(siete_segmentos_2_f), .a(siete_segmentos_2_a), .b(siete_segmentos_2_b),
    .e(siete_segmentos_2_e), .d(siete_segmentos_2_d), .c(siete_segmentos_2_c));  // open: dp
endmodule

module primeraSecuencia (
  input  X,
  input  CLK,
  input  Reset,
  output Z,
  output [2:0] S1
);

  wire and_4_out, not_1_out, R0, R1, R2, S0, S1_t, S2;

  not not_1 (not_1_out, S1[1]);
  not not_2 (R2, S1[0]);
  not not_3 (R1, X);
  and and_1 (S2, S1[1], S1[0], R1);
  and and_2 (S1_t, S1[0], X);
  and and_3 (S0, R2, X);
  and and_4 (and_4_out, not_1_out, S1[0]);
  or or_1 (R0, and_4_out, R1);
  LED led_1 (.in(S1[2]));
  S_R_Flip_Flop s_r_ff_1 (.S(S2), .R(R2), .clk(CLK), .Q(S1[2]), .reset(Reset));  // open: Qn, preset
  S_R_Flip_Flop s_r_ff_2 (.S(S1_t), .R(R1), .clk(CLK), .Q(S1[1]), .reset(Reset));  // open: Qn, preset
  S_R_Flip_Flop s_r_ff_3 (.S(S0), .R(R0), .clk(CLK), .Q(S1[0]), .reset(Reset));  // open: Qn, preset
  // Probe on S1

  assign Z = S1[2];

  // Other names for the same wires on the sheet: Q0 = S1[0]; Q1 = S1[1]; Q2 = S1[2]
endmodule

module segundaSecuencia (
  input  X,
  input  CLK,
  input  Reset,
  output [2:0] S2,
  output Z
);

  wire and_2_out, and_3_out, and_4_out, and_5_out, and_6_out, and_7_out, and_8_out, and_9_out, and_10_out,
       and_11_out, not_1_out, not_2_out, not_3_out, R0, R1, R2, S0, S1, S2_t;

  not not_1 (not_1_out, S2[2]);
  not not_2 (not_2_out, S2[0]);
  not not_3 (not_3_out, X);
  and and_1 (S2_t, S2[1], S2[0], X);
  and and_2 (and_2_out, S2[2], X);
  and and_3 (and_3_out, S2[2], S2[0]);
  and and_4 (and_4_out, not_1_out, S2[0], not_3_out);
  and and_5 (and_5_out, S2[2], S2[0], X);
  and and_6 (and_6_out, not_2_out, not_3_out);
  and and_7 (and_7_out, not_1_out, S2[0], X);
  and and_8 (and_8_out, not_2_out, X);
  and and_9 (and_9_out, S2[2], not_2_out);
  and and_10 (and_10_out, S2[0], not_3_out);
  and and_11 (and_11_out, S2[1], S2[0]);
  and and_12 (Z, S2[2], S2[0]);
  or or_1 (R2, and_2_out, and_3_out);
  or or_2 (S1, and_4_out, and_5_out);
  or or_3 (R1, and_6_out, and_7_out);
  or or_4 (S0, and_8_out, and_9_out);
  or or_5 (R0, and_10_out, and_11_out);
  LED led_1 (.in(Z));
  S_R_Flip_Flop s_r_ff_1 (.S(S2_t), .R(R2), .clk(CLK), .Q(S2[2]), .reset(Reset));  // open: Qn, preset
  S_R_Flip_Flop s_r_ff_2 (.S(S1), .R(R1), .clk(CLK), .Q(S2[1]), .reset(Reset));  // open: Qn, preset
  S_R_Flip_Flop s_r_ff_3 (.S(S0), .R(R0), .clk(CLK), .Q(S2[0]), .reset(Reset));  // open: Qn, preset
  // Probe on S2

  // Other names for the same wires on the sheet: Q0 = S2[0]; Q1 = S2[1]; Q2 = S2[2]
endmodule

module terceraSecuencia (
  input  X,
  input  CLK,
  input  Reset,
  output [2:0] S3,
  output Z
);

  wire and_2_out, and_3_out, and_4_out, and_5_out, and_6_out, and_7_out, and_8_out, and_9_out, and_10_out,
       not_1_out, not_2_out, not_3_out, not_4_out, R0, R1, R2, S0, S1, S2;

  not not_1 (not_1_out, S3[2]);
  not not_2 (not_2_out, S3[1]);
  not not_3 (not_3_out, S3[0]);
  not not_4 (not_4_out, X);
  and and_1 (S2, S3[1], S3[0], X);
  and and_2 (and_2_out, S3[1], not_3_out);
  and and_3 (and_3_out, not_1_out, S3[0], not_4_out);
  and and_4 (and_4_out, S3[2], S3[0], X);
  and and_5 (and_5_out, not_1_out, X);
  and and_6 (and_6_out, S3[2], not_3_out);
  and and_7 (and_7_out, not_3_out, not_4_out);
  and and_8 (and_8_out, S3[2], not_2_out, not_3_out);
  and and_9 (and_9_out, not_1_out, not_2_out, S3[0]);
  and and_10 (and_10_out, S3[0], X);
  and and_11 (Z, S3[2], S3[1]);
  or or_1 (R2, and_2_out, not_4_out);
  or or_2 (S1, and_3_out, and_4_out);
  or or_3 (R1, and_5_out, and_6_out);
  or or_4 (S0, and_7_out, and_8_out);
  or or_5 (R0, and_9_out, and_10_out);
  LED led_1 (.in(Z));
  S_R_Flip_Flop s_r_ff_1 (.S(S2), .R(R2), .clk(CLK), .Q(S3[2]), .reset(Reset));  // open: Qn, preset
  S_R_Flip_Flop s_r_ff_2 (.S(S1), .R(R1), .clk(CLK), .Q(S3[1]), .reset(Reset));  // open: Qn, preset
  S_R_Flip_Flop s_r_ff_3 (.S(S0), .R(R0), .clk(CLK), .Q(S3[0]), .reset(Reset));  // open: Qn, preset
  // Probe on S3

  // Other names for the same wires on the sheet: Q0 = S3[0]; Q1 = S3[1]; Q2 = S3[2]
endmodule

module unionSecuencias1_2 (
  input  X
);

  wire and_2_out, and_3_out, and_4_out, and_5_out, and_6_out, and_7_out, and_8_out, and_9_out, and_10_out,
       and_11_out, and_12_out, and_13_out, and_14_out, and_15_out, and_16_out, button_1_out, clock_1_out,
       not_1_out, not_2_out, not_4_out, not_5_out, or_1_out, or_2_out, or_3_out, or_4_out, Q0, Q1, Q2, Q3,
       R0, R1, R2, R3, S0, S1, S2, S3, Z1;

  not not_1 (not_1_out, Q3);
  not not_2 (not_2_out, Q2);
  not not_3 (R3, Q1);
  not not_4 (not_4_out, Q0);
  not not_5 (not_5_out, X);
  and and_1 (S3, Q2, Q1, Q0, not_5_out);
  and and_2 (and_2_out, Q1, X);
  and and_3 (and_3_out, Q3, X);
  and and_4 (and_4_out, Q0, not_5_out);
  and and_5 (and_5_out, Q1, not_5_out);
  and and_6 (and_6_out, not_2_out, R3, Q0);
  and and_7 (and_7_out, R3, Q0, X);
  and and_8 (and_8_out, not_2_out, not_4_out, not_5_out);
  and and_9 (and_9_out, Q1, Q0, X);
  and and_10 (and_10_out, Q2, Q0, not_5_out);
  and and_11 (and_11_out, not_1_out, not_2_out, R3, X);
  and and_12 (and_12_out, Q2, R3, not_4_out, not_5_out);
  and and_13 (and_13_out, Q2, Q1, not_4_out, X);
  and and_14 (and_14_out, Q0, not_5_out);
  and and_15 (and_15_out, Q1, Q0);
  and and_16 (and_16_out, Q2, Q0);
  and and_17 (Z1, Q2, R3, Q0);
  or or_1 (or_1_out, and_8_out, and_9_out);
  or or_2 (or_2_out, and_10_out, Q3);
  or or_3 (or_3_out, and_11_out, and_12_out);
  or or_4 (or_4_out, and_14_out, and_15_out);
  or or_5 (S2, and_2_out, and_3_out);
  or or_6 (R2, and_4_out, and_5_out);
  or or_7 (S1, and_6_out, and_7_out);
  or or_8 (R1, or_1_out, or_2_out);
  or or_9 (S0, or_3_out, and_13_out);
  or or_10 (R0, or_4_out, and_16_out);
  LED led_1 (.in(Z1));
  LED led_2 (.in(Q3));
  Clock clock_1 (.out(clock_1_out));
  Button button_1 (.out(button_1_out));
  // Probe on {Q3, Q2, Q1, Q0}
  S_R_Flip_Flop s_r_ff_1 (.S(S3), .R(R3), .clk(clock_1_out), .Q(Q3), .reset(button_1_out));  // open: Qn, preset
  S_R_Flip_Flop s_r_ff_2 (.S(S2), .R(R2), .clk(clock_1_out), .Q(Q2), .reset(button_1_out));  // open: Qn, preset
  S_R_Flip_Flop s_r_ff_3 (.S(S1), .R(R1), .clk(clock_1_out), .Q(Q1), .reset(button_1_out));  // open: Qn, preset
  S_R_Flip_Flop s_r_ff_4 (.S(S0), .R(R0), .clk(clock_1_out), .Q(Q0), .reset(button_1_out));  // open: Qn, preset

  // Other names for the same wires on the sheet: Z2 = Q3
endmodule

module contador_4bits (
  input  X,
  input  clk,
  input  reset,
  output Q3,
  output Q2,
  output Q1,
  output Q0
);

  wire not_1_out, not_2_out, not_3_out, not_4_out, R0, R1, R2, R3, S0, S1, S2, S3;

  not not_1 (not_1_out, Q3);
  not not_2 (not_2_out, Q2);
  not not_3 (not_3_out, Q1);
  S_R_Flip_Flop FF3 (.S(S3), .R(R3), .clk(clk), .Q(Q3), .reset(reset));  // open: Qn, preset
  not not_4 (not_4_out, Q0);
  S_R_Flip_Flop FF2 (.S(S2), .R(R2), .clk(clk), .Q(Q2), .reset(reset));  // open: Qn, preset
  and and_1 (S3, not_1_out, Q2, Q1, Q0, X);
  and and_2 (R3, Q3, Q2, Q1, Q0, X);
  and and_3 (S2, not_2_out, Q1, Q0, X);
  and and_4 (R2, Q2, Q1, Q0, X);
  and and_5 (S1, not_3_out, Q0, X);
  and and_6 (R1, Q1, Q0, X);
  and and_7 (S0, not_4_out, X);
  and and_8 (R0, Q0, X);
  S_R_Flip_Flop FF1 (.S(S1), .R(R1), .clk(clk), .Q(Q1), .reset(reset));  // open: Qn, preset
  S_R_Flip_Flop FF0 (.S(S0), .R(R0), .clk(clk), .Q(Q0), .reset(reset));  // open: Qn, preset
  // Probe on {Q3, Q2, Q1, Q0}
endmodule

module contadorJK (
  input  X,
  input  CLK,
  input  Reset,
  output Q0,
  output Q1,
  output Q2,
  output Q3,
  output Q4,
  output Q5,
  output Q6,
  output Q7
);

  J_K_Flip_Flop #(.trigger("falling")) j_k_ff_1 (.J(X), .K(X), .clk(CLK), .Q(Q0), .reset(Reset));  // open: Qn, preset
  // Probe on {Q7, Q6, Q5, Q4, Q3, Q2, Q1, Q0}
  J_K_Flip_Flop #(.trigger("falling")) j_k_ff_2 (.J(X), .K(X), .clk(Q0), .Q(Q1), .reset(Reset));  // open: Qn, preset
  J_K_Flip_Flop #(.trigger("falling")) j_k_ff_3 (.J(X), .K(X), .clk(Q1), .Q(Q2), .reset(Reset));  // open: Qn, preset
  J_K_Flip_Flop #(.trigger("falling")) j_k_ff_4 (.J(X), .K(X), .clk(Q2), .Q(Q3), .reset(Reset));  // open: Qn, preset
  J_K_Flip_Flop #(.trigger("falling")) j_k_ff_5 (.J(X), .K(X), .clk(Q3), .Q(Q4), .reset(Reset));  // open: Qn, preset
  J_K_Flip_Flop #(.trigger("falling")) j_k_ff_6 (.J(X), .K(X), .clk(Q4), .Q(Q5), .reset(Reset));  // open: Qn, preset
  J_K_Flip_Flop #(.trigger("falling")) j_k_ff_7 (.J(X), .K(X), .clk(Q5), .Q(Q6), .reset(Reset));  // open: Qn, preset
  J_K_Flip_Flop #(.trigger("falling")) j_k_ff_8 (.J(X), .K(X), .clk(Q6), .Q(Q7), .reset(Reset));  // open: Qn, preset
endmodule

module contador8bits_SR (
  input  X,
  input  CLK,
  input  Reset,
  output [7:0] Cn
);

  wire and_1_out;

  // Probe on Cn
  contador_4bits contador_4bits_1 (.X(X), .clk(CLK), .reset(Reset), .Q3(Cn[3]), .Q2(Cn[2]), .Q1(Cn[1]), .Q0(Cn[0]));
  and and_1 (and_1_out, Cn[3], Cn[2], Cn[1], Cn[0]);
  contador_4bits contador_4bits_2 (
    .X(and_1_out), .clk(CLK), .reset(Reset), .Q3(Cn[7]), .Q2(Cn[6]), .Q1(Cn[5]), .Q0(Cn[4]));

  // Other names for the same wires on the sheet: Q0 = Cn[0]; Q1 = Cn[1]; Q2 = Cn[2]; Q3 = Cn[3]; Q4 = Cn[4];
  //   Q5 = Cn[5]; Q6 = Cn[6]; Q7 = Cn[7]
endmodule

module TresSeq_Individual (
  input  in_1
);

  wire button_1_out, clock_1_out, primerasecuencia_1_z, segundasecuencia_1_z, siete_segmentos_1_a,
       siete_segmentos_1_b, siete_segmentos_1_c, siete_segmentos_1_d, siete_segmentos_1_e,
       siete_segmentos_1_f, siete_segmentos_1_g, siete_segmentos_2_a, siete_segmentos_2_b,
       siete_segmentos_2_c, siete_segmentos_2_d, siete_segmentos_2_e, siete_segmentos_2_f,
       siete_segmentos_2_g, siete_segmentos_3_a, siete_segmentos_3_b, siete_segmentos_3_c,
       siete_segmentos_3_d, siete_segmentos_3_e, siete_segmentos_3_f, siete_segmentos_3_g,
       siete_segmentos_4_a, siete_segmentos_4_b, siete_segmentos_4_c, siete_segmentos_4_d,
       siete_segmentos_4_e, siete_segmentos_4_f, siete_segmentos_4_g, siete_segmentos_5_a,
       siete_segmentos_5_b, siete_segmentos_5_c, siete_segmentos_5_d, siete_segmentos_5_e,
       siete_segmentos_5_f, siete_segmentos_5_g, siete_segmentos_6_a, siete_segmentos_6_b,
       siete_segmentos_6_c, siete_segmentos_6_d, siete_segmentos_6_e, siete_segmentos_6_f,
       siete_segmentos_6_g, siete_segmentos_7_a, siete_segmentos_7_b, siete_segmentos_7_c,
       siete_segmentos_7_d, siete_segmentos_7_e, siete_segmentos_7_f, siete_segmentos_7_g,
       siete_segmentos_8_a, siete_segmentos_8_b, siete_segmentos_8_c, siete_segmentos_8_d,
       siete_segmentos_8_e, siete_segmentos_8_f, siete_segmentos_8_g, siete_segmentos_9_a,
       siete_segmentos_9_b, siete_segmentos_9_c, siete_segmentos_9_d, siete_segmentos_9_e,
       siete_segmentos_9_f, siete_segmentos_9_g, sieteseg3bits_1_a, sieteseg3bits_1_b, sieteseg3bits_1_c,
       sieteseg3bits_1_d, sieteseg3bits_1_e, sieteseg3bits_1_f, sieteseg3bits_1_g, sieteseg3bits_2_a,
       sieteseg3bits_2_b, sieteseg3bits_2_c, sieteseg3bits_2_d, sieteseg3bits_2_e, sieteseg3bits_2_f,
       sieteseg3bits_2_g, sieteseg3bits_3_a, sieteseg3bits_3_b, sieteseg3bits_3_c, sieteseg3bits_3_d,
       sieteseg3bits_3_e, sieteseg3bits_3_f, sieteseg3bits_3_g, tercerasecuencia_1_z;
  wire [2:0] S1, S2, S3;
  wire [3:0] bcd_1_c, bcd_1_d, bcd_1_u, bcd_2_c, bcd_2_d, bcd_2_u, bcd_3_c, bcd_3_d, bcd_3_u;
  wire [7:0] C1, C2, C3;

  Clock clock_1 (.out(clock_1_out));
  Button button_1 (.out(button_1_out));
  primeraSecuencia primerasecuencia_1 (
    .X(in_1), .CLK(clock_1_out), .Reset(button_1_out), .Z(primerasecuencia_1_z), .S1(S1));
  // Probe on S1
  LED led_1 (.in(primerasecuencia_1_z));
  LED led_2 (.in(segundasecuencia_1_z));
  BCD bcd_1 (.Count(C1), .c(bcd_1_c), .u(bcd_1_u), .d(bcd_1_d));
  BCD bcd_2 (.Count(C2), .c(bcd_2_c), .u(bcd_2_u), .d(bcd_2_d));
  BCD bcd_3 (.Count(C3), .c(bcd_3_c), .u(bcd_3_u), .d(bcd_3_d));
  segundaSecuencia segundasecuencia_1 (
    .X(in_1), .CLK(clock_1_out), .Reset(button_1_out), .S2(S2), .Z(segundasecuencia_1_z));
  // Probe on S2
  terceraSecuencia tercerasecuencia_1 (
    .X(in_1), .CLK(clock_1_out), .Reset(button_1_out), .S3(S3), .Z(tercerasecuencia_1_z));
  LED led_3 (.in(tercerasecuencia_1_z));
  // Probe on S3
  siete_segmentos siete_segmentos_1 (
    .W(bcd_1_c[3]), .X(bcd_1_c[2]), .Y(bcd_1_c[1]), .Z(bcd_1_c[0]), .A(siete_segmentos_1_a),
    .B(siete_segmentos_1_b), .C(siete_segmentos_1_c), .D(siete_segmentos_1_d), .E(siete_segmentos_1_e),
    .F(siete_segmentos_1_f), .G(siete_segmentos_1_g));
  siete_segmentos siete_segmentos_2 (
    .W(bcd_2_c[3]), .X(bcd_2_c[2]), .Y(bcd_2_c[1]), .Z(bcd_2_c[0]), .A(siete_segmentos_2_a),
    .B(siete_segmentos_2_b), .C(siete_segmentos_2_c), .D(siete_segmentos_2_d), .E(siete_segmentos_2_e),
    .F(siete_segmentos_2_f), .G(siete_segmentos_2_g));
  siete_segmentos siete_segmentos_3 (
    .W(bcd_3_c[3]), .X(bcd_3_c[2]), .Y(bcd_3_c[1]), .Z(bcd_3_c[0]), .A(siete_segmentos_3_a),
    .B(siete_segmentos_3_b), .C(siete_segmentos_3_c), .D(siete_segmentos_3_d), .E(siete_segmentos_3_e),
    .F(siete_segmentos_3_f), .G(siete_segmentos_3_g));
  _7_Segment_Display u_7_segment_display_1 (
    .g(siete_segmentos_1_g), .f(siete_segmentos_1_f), .a(siete_segmentos_1_a), .b(siete_segmentos_1_b),
    .e(siete_segmentos_1_e), .d(siete_segmentos_1_d), .c(siete_segmentos_1_c));  // open: dp
  _7_Segment_Display u_7_segment_display_2 (
    .g(siete_segmentos_2_g), .f(siete_segmentos_2_f), .a(siete_segmentos_2_a), .b(siete_segmentos_2_b),
    .e(siete_segmentos_2_e), .d(siete_segmentos_2_d), .c(siete_segmentos_2_c));  // open: dp
  _7_Segment_Display u_7_segment_display_3 (
    .g(siete_segmentos_3_g), .f(siete_segmentos_3_f), .a(siete_segmentos_3_a), .b(siete_segmentos_3_b),
    .e(siete_segmentos_3_e), .d(siete_segmentos_3_d), .c(siete_segmentos_3_c));  // open: dp
  siete_segmentos siete_segmentos_4 (
    .W(bcd_1_d[3]), .X(bcd_1_d[2]), .Y(bcd_1_d[1]), .Z(bcd_1_d[0]), .A(siete_segmentos_4_a),
    .B(siete_segmentos_4_b), .C(siete_segmentos_4_c), .D(siete_segmentos_4_d), .E(siete_segmentos_4_e),
    .F(siete_segmentos_4_f), .G(siete_segmentos_4_g));
  siete_segmentos siete_segmentos_5 (
    .W(bcd_2_d[3]), .X(bcd_2_d[2]), .Y(bcd_2_d[1]), .Z(bcd_2_d[0]), .A(siete_segmentos_5_a),
    .B(siete_segmentos_5_b), .C(siete_segmentos_5_c), .D(siete_segmentos_5_d), .E(siete_segmentos_5_e),
    .F(siete_segmentos_5_f), .G(siete_segmentos_5_g));
  siete_segmentos siete_segmentos_6 (
    .W(bcd_3_d[3]), .X(bcd_3_d[2]), .Y(bcd_3_d[1]), .Z(bcd_3_d[0]), .A(siete_segmentos_6_a),
    .B(siete_segmentos_6_b), .C(siete_segmentos_6_c), .D(siete_segmentos_6_d), .E(siete_segmentos_6_e),
    .F(siete_segmentos_6_f), .G(siete_segmentos_6_g));
  contador8bits_SR contador8bits_sr_1 (.X(tercerasecuencia_1_z), .CLK(clock_1_out), .Reset(button_1_out), .Cn(C3));
  contador8bits_SR contador8bits_sr_2 (.X(segundasecuencia_1_z), .CLK(clock_1_out), .Reset(button_1_out), .Cn(C2));
  contador8bits_SR contador8bits_sr_3 (.X(primerasecuencia_1_z), .CLK(clock_1_out), .Reset(button_1_out), .Cn(C1));
  _7_Segment_Display u_7_segment_display_4 (
    .g(siete_segmentos_4_g), .f(siete_segmentos_4_f), .a(siete_segmentos_4_a), .b(siete_segmentos_4_b),
    .e(siete_segmentos_4_e), .d(siete_segmentos_4_d), .c(siete_segmentos_4_c));  // open: dp
  _7_Segment_Display u_7_segment_display_5 (
    .g(siete_segmentos_5_g), .f(siete_segmentos_5_f), .a(siete_segmentos_5_a), .b(siete_segmentos_5_b),
    .e(siete_segmentos_5_e), .d(siete_segmentos_5_d), .c(siete_segmentos_5_c));  // open: dp
  _7_Segment_Display u_7_segment_display_6 (
    .g(siete_segmentos_6_g), .f(siete_segmentos_6_f), .a(siete_segmentos_6_a), .b(siete_segmentos_6_b),
    .e(siete_segmentos_6_e), .d(siete_segmentos_6_d), .c(siete_segmentos_6_c));  // open: dp
  siete_segmentos siete_segmentos_7 (
    .W(bcd_1_u[3]), .X(bcd_1_u[2]), .Y(bcd_1_u[1]), .Z(bcd_1_u[0]), .A(siete_segmentos_7_a),
    .B(siete_segmentos_7_b), .C(siete_segmentos_7_c), .D(siete_segmentos_7_d), .E(siete_segmentos_7_e),
    .F(siete_segmentos_7_f), .G(siete_segmentos_7_g));
  siete_segmentos siete_segmentos_8 (
    .W(bcd_2_u[3]), .X(bcd_2_u[2]), .Y(bcd_2_u[1]), .Z(bcd_2_u[0]), .A(siete_segmentos_8_a),
    .B(siete_segmentos_8_b), .C(siete_segmentos_8_c), .D(siete_segmentos_8_d), .E(siete_segmentos_8_e),
    .F(siete_segmentos_8_f), .G(siete_segmentos_8_g));
  siete_segmentos siete_segmentos_9 (
    .W(bcd_3_u[3]), .X(bcd_3_u[2]), .Y(bcd_3_u[1]), .Z(bcd_3_u[0]), .A(siete_segmentos_9_a),
    .B(siete_segmentos_9_b), .C(siete_segmentos_9_c), .D(siete_segmentos_9_d), .E(siete_segmentos_9_e),
    .F(siete_segmentos_9_f), .G(siete_segmentos_9_g));
  _7_Segment_Display u_7_segment_display_7 (
    .g(siete_segmentos_7_g), .f(siete_segmentos_7_f), .a(siete_segmentos_7_a), .b(siete_segmentos_7_b),
    .e(siete_segmentos_7_e), .d(siete_segmentos_7_d), .c(siete_segmentos_7_c));  // open: dp
  _7_Segment_Display u_7_segment_display_8 (
    .g(siete_segmentos_8_g), .f(siete_segmentos_8_f), .a(siete_segmentos_8_a), .b(siete_segmentos_8_b),
    .e(siete_segmentos_8_e), .d(siete_segmentos_8_d), .c(siete_segmentos_8_c));  // open: dp
  _7_Segment_Display u_7_segment_display_9 (
    .g(siete_segmentos_9_g), .f(siete_segmentos_9_f), .a(siete_segmentos_9_a), .b(siete_segmentos_9_b),
    .e(siete_segmentos_9_e), .d(siete_segmentos_9_d), .c(siete_segmentos_9_c));  // open: dp
  sieteSeg3Bits sieteseg3bits_1 (
    .X(S1[2]), .Y(S1[1]), .Z(S1[0]), .A(sieteseg3bits_1_a), .B(sieteseg3bits_1_b), .C(sieteseg3bits_1_c),
    .D(sieteseg3bits_1_d), .E(sieteseg3bits_1_e), .F(sieteseg3bits_1_f), .G(sieteseg3bits_1_g));
  sieteSeg3Bits sieteseg3bits_2 (
    .X(S2[2]), .Y(S2[1]), .Z(S2[0]), .A(sieteseg3bits_2_a), .B(sieteseg3bits_2_b), .C(sieteseg3bits_2_c),
    .D(sieteseg3bits_2_d), .E(sieteseg3bits_2_e), .F(sieteseg3bits_2_f), .G(sieteseg3bits_2_g));
  sieteSeg3Bits sieteseg3bits_3 (
    .X(S3[2]), .Y(S3[1]), .Z(S3[0]), .A(sieteseg3bits_3_a), .B(sieteseg3bits_3_b), .C(sieteseg3bits_3_c),
    .D(sieteseg3bits_3_d), .E(sieteseg3bits_3_e), .F(sieteseg3bits_3_f), .G(sieteseg3bits_3_g));
  _7_Segment_Display u_7_segment_display_10 (
    .g(sieteseg3bits_1_g), .f(sieteseg3bits_1_f), .a(sieteseg3bits_1_a), .b(sieteseg3bits_1_b),
    .e(sieteseg3bits_1_e), .d(sieteseg3bits_1_d), .c(sieteseg3bits_1_c));  // open: dp
  _7_Segment_Display u_7_segment_display_11 (
    .g(sieteseg3bits_2_g), .f(sieteseg3bits_2_f), .a(sieteseg3bits_2_a), .b(sieteseg3bits_2_b),
    .e(sieteseg3bits_2_e), .d(sieteseg3bits_2_d), .c(sieteseg3bits_2_c));  // open: dp
  _7_Segment_Display u_7_segment_display_12 (
    .g(sieteseg3bits_3_g), .f(sieteseg3bits_3_f), .a(sieteseg3bits_3_a), .b(sieteseg3bits_3_b),
    .e(sieteseg3bits_3_e), .d(sieteseg3bits_3_d), .c(sieteseg3bits_3_c));  // open: dp
endmodule

module sieteSeg3Bits (
  input  X,
  input  Y,
  input  Z,
  output A,
  output B,
  output C,
  output D,
  output E,
  output F,
  output G
);

  wire and_1_out, and_2_out, and_3_out, and_4_out, and_5_out, and_6_out, and_7_out, and_8_out, and_9_out,
       and_10_out, and_11_out, and_12_out, and_13_out, and_14_out, and_15_out, and_16_out, not_1_out,
       not_2_out, not_3_out, or_2_out, or_3_out, or_4_out, or_5_out, or_6_out, or_7_out;

  not not_1 (not_1_out, X);
  not not_2 (not_2_out, Y);
  not not_3 (not_3_out, Z);
  and and_1 (and_1_out, not_1_out, not_3_out);
  and and_2 (and_2_out, X, Z);
  and and_3 (and_3_out, Y, Z);
  and and_4 (and_4_out, not_2_out, not_3_out);
  or or_1 (C, not_2_out, Z, X);
  and and_5 (and_5_out, not_1_out, not_3_out);
  and and_6 (and_6_out, not_1_out, Y);
  and and_7 (and_7_out, Y, not_3_out);
  and and_8 (and_8_out, X, not_2_out, Z);
  and and_9 (and_9_out, not_1_out, not_3_out);
  and and_10 (and_10_out, Y, not_3_out);
  and and_11 (and_11_out, not_2_out, not_3_out);
  and and_12 (and_12_out, X, not_3_out);
  and and_13 (and_13_out, X, not_2_out);
  and and_14 (and_14_out, Y, not_3_out);
  and and_15 (and_15_out, not_1_out, Y);
  and and_16 (and_16_out, X, not_2_out);
  or or_2 (or_2_out, and_1_out, and_2_out);
  or or_3 (or_3_out, and_3_out, and_4_out);
  or or_4 (or_4_out, and_5_out, and_6_out);
  or or_5 (or_5_out, and_7_out, and_8_out);
  or or_6 (or_6_out, and_11_out, and_12_out);
  or or_7 (or_7_out, and_14_out, and_15_out);
  or or_8 (F, or_6_out, and_13_out);
  or or_9 (G, or_7_out, and_16_out);
  or or_10 (A, Y, or_2_out);
  or or_11 (B, or_3_out, not_1_out);
  or or_12 (D, or_4_out, or_5_out);
  or or_13 (E, and_9_out, and_10_out);
endmodule

module tresSecuenciasUnion (
  input  X,
  input  CLK,
  input  Reset,
  output [3:0] Sn,
  output Z1,
  output Z2,
  output Z3
);

  wire and_1_out, and_2_out, and_3_out, and_4_out, and_5_out, and_6_out, and_7_out, and_8_out, and_9_out,
       and_10_out, and_11_out, and_12_out, and_13_out, and_14_out, and_15_out, and_16_out, and_17_out,
       and_18_out, and_19_out, and_20_out, and_21_out, and_22_out, and_23_out, and_24_out, and_25_out,
       and_26_out, and_27_out, and_28_out, and_29_out, and_30_out, and_31_out, and_32_out, and_33_out,
       not_1_out, not_2_out, not_3_out, not_4_out, not_5_out, not_6_out, not_7_out, not_8_out, not_9_out,
       not_10_out, or_2_out, or_3_out, or_4_out, or_5_out, or_6_out, or_7_out, or_9_out, or_13_out,
       or_17_out, or_18_out, or_19_out, or_20_out, or_21_out, or_22_out, or_23_out, or_24_out, or_25_out, R0,
       R1, R2, R3, S0, S1, S2, S3;

  not not_1 (not_1_out, Sn[3]);
  S_R_Flip_Flop s_r_ff_1 (.S(S3), .R(R3), .clk(CLK), .Q(Sn[3]), .reset(Reset));  // open: Qn, preset
  not not_2 (not_2_out, Sn[2]);
  not not_3 (not_3_out, Sn[1]);
  not not_4 (not_4_out, Sn[0]);
  S_R_Flip_Flop s_r_ff_2 (.S(S2), .R(R2), .clk(CLK), .Q(Sn[2]), .reset(Reset));  // open: Qn, preset
  not not_5 (not_5_out, X);
  S_R_Flip_Flop s_r_ff_3 (.S(S1), .R(R1), .clk(CLK), .Q(Sn[1]), .reset(Reset));  // open: Qn, preset
  and and_1 (and_1_out, Sn[2], Sn[1], X);
  and and_2 (and_2_out, not_1_out, Sn[2], Sn[0], X);
  and and_3 (and_3_out, Sn[0], not_5_out);
  and and_4 (and_4_out, Sn[3], Sn[1], Sn[0]);
  and and_5 (and_5_out, Sn[3], Sn[2], Sn[0]);
  and and_6 (and_6_out, Sn[2], not_3_out, not_5_out);
  and and_7 (and_7_out, not_1_out, not_2_out, Sn[1], not_4_out);
  and and_8 (and_8_out, not_2_out, Sn[1], not_4_out, not_5_out);
  and and_9 (and_9_out, not_1_out, Sn[1], Sn[0], not_5_out);
  and and_10 (and_10_out, Sn[3], not_2_out, not_3_out, Sn[0]);
  and and_11 (and_11_out, Sn[3], Sn[0], X);
  and and_12 (and_12_out, Sn[2], Sn[1], not_4_out);
  and and_13 (and_13_out, not_1_out, Sn[2], not_4_out, not_5_out);
  and and_14 (and_14_out, not_1_out, Sn[0], X);
  and and_15 (and_15_out, Sn[3], Sn[2], Sn[0], not_5_out);
  or or_1 (S3, and_1_out, and_2_out);
  or or_2 (or_2_out, and_3_out, and_4_out);
  or or_3 (or_3_out, and_5_out, and_6_out);
  or or_4 (or_4_out, and_7_out, and_8_out);
  or or_5 (or_5_out, and_10_out, and_11_out);
  or or_6 (or_6_out, and_12_out, and_13_out);
  LED led_1 (.in(Z1));
  LED led_2 (.in(Z2));
  LED led_3 (.in(Z3));
  or or_7 (or_7_out, and_14_out, and_15_out);
  S_R_Flip_Flop s_r_ff_4 (.S(S0), .R(R0), .clk(CLK), .Q(Sn[0]), .reset(Reset));  // open: Qn, preset
  or or_8 (R3, or_2_out, or_3_out);
  or or_9 (or_9_out, and_9_out, or_5_out);
  or or_10 (R2, or_6_out, or_7_out);
  or or_11 (S1, or_17_out, or_13_out);
  or or_12 (S2, or_4_out, or_9_out);
  or or_13 (or_13_out, or_18_out, or_19_out);
  or or_14 (R1, and_22_out, or_20_out);
  or or_15 (S0, or_21_out, or_22_out);
  or or_16 (R0, or_23_out, or_25_out);
  or or_17 (or_17_out, and_16_out, and_17_out);
  or or_18 (or_18_out, and_18_out, and_19_out);
  or or_19 (or_19_out, and_20_out, and_21_out);
  or or_20 (or_20_out, and_23_out, and_24_out);
  or or_21 (or_21_out, and_25_out, and_26_out);
  or or_22 (or_22_out, and_27_out, and_28_out);
  or or_23 (or_23_out, and_29_out, and_30_out);
  or or_24 (or_24_out, and_31_out, and_32_out);
  or or_25 (or_25_out, or_24_out, and_33_out);
  and and_16 (and_16_out, not_6_out, not_7_out, Sn[0]);
  and and_17 (and_17_out, not_6_out, not_7_out, not_8_out, X);
  and and_18 (and_18_out, not_6_out, Sn[2], not_8_out, not_9_out);
  and and_19 (and_19_out, Sn[3], not_7_out, not_8_out, not_9_out, not_10_out);
  and and_20 (and_20_out, Sn[3], Sn[2], not_8_out, X);
  and and_21 (and_21_out, Sn[3], Sn[2], Sn[0]);
  and and_22 (and_22_out, Sn[1], not_9_out, X);
  and and_23 (and_23_out, not_7_out, Sn[1], not_9_out);
  and and_24 (and_24_out, not_6_out, Sn[2], Sn[1], not_10_out);
  and and_25 (and_25_out, not_7_out, not_8_out, not_9_out, not_10_out);
  and and_26 (and_26_out, not_6_out, Sn[1], not_9_out, X);
  and and_27 (and_27_out, not_6_out, Sn[2], not_9_out);
  and and_28 (and_28_out, Sn[3], Sn[1], not_10_out);
  and and_29 (and_29_out, not_6_out, Sn[0], X);
  and and_30 (and_30_out, not_6_out, Sn[2], Sn[0]);
  and and_31 (and_31_out, not_6_out, Sn[1], Sn[0]);
  and and_32 (and_32_out, Sn[3], not_9_out, X);
  and and_33 (and_33_out, Sn[3], not_7_out, not_8_out, Sn[0]);
  and and_34 (Z1, Sn[3], Sn[1], Sn[0]);
  and and_35 (Z2, Sn[3], Sn[2], Sn[0]);
  and and_36 (Z3, Sn[3], Sn[2], Sn[1]);
  not not_6 (not_6_out, Sn[3]);
  not not_7 (not_7_out, Sn[2]);
  not not_8 (not_8_out, Sn[1]);
  not not_9 (not_9_out, Sn[0]);
  not not_10 (not_10_out, X);

  // Other names for the same wires on the sheet: Q0 = Sn[0]; Q1 = Sn[1]; Q2 = Sn[2]; Q3 = Sn[3]
endmodule
