// Logisim project Practica03.circ as structural Verilog: 16 circuits, main circuit main
module main (
);

  wire alu_1_zero, ALUSrc, and_1_out, ANDi, Branch, CLK, jal_control, jr_check, lhu, MemRead, MemtoReg,
       MemWrite, RegDst, RegWrite, Reset;
  wire [1:0] ALUop;
  wire [2:0] alucontrol_1_op;
  wire [4:0] multiplexer_1_out, rd, rs, rt, shamt;
  wire [5:0] funct, op;
  wire [15:0] imm;
  wire [25:0] address;
  wire [31:0] adder_1_out, alu_1_result, data_memory_1_memoutput, fetch_1_instruction, fetch_1_pc,
       Jump_Address, multiplexer_2_out, multiplexer_3_out, multiplexer_4_out, PCnext, PCplus4,
       reg_file_1_read_data1, reg_file_1_read_data2, shift_left2_1_out32bit, sign_ext_1_out32bit, Write_data;

  Clock u_CLK (.out(CLK));
  Button u_Reset (.out(Reset));
  // Probe on fetch_1_pc
  Fetch fetch_1 (
    .PCnext(PCnext), .CLK(CLK), .Reset(Reset), .PC(fetch_1_pc), .PCplus4(PCplus4),
    .Instruction(fetch_1_instruction));
  Ildown ildown_1 (
    .Instruction(fetch_1_instruction), .address(address), .imm(imm), .funct(funct), .shamt(shamt), .rd(rd),
    .rt(rt), .rs(rs), .op(op));
  control_v2 control_v2_1 (
    .Op(op), .RegDst(RegDst), .ALUSrc(ALUSrc), .MemtoReg(MemtoReg), .RegWrite(RegWrite), .MemRead(MemRead),
    .MemWrite(MemWrite), .Branch(Branch), .ALUOp(ALUop), .lhu(lhu), .andi(ANDi), .jal(jal_control));
  Multiplexer #(.width(5)) multiplexer_1 (.in0(rt), .in1(rd), .out(multiplexer_1_out), .sel(RegDst));
  jal jal_1 (.Instruction(address), .PCplus4(PCplus4), .Jump_Address(Jump_Address));
  jr jr_1 (.Op(funct), .ALUop(ALUop), .jr_check(jr_check));
  Reg_File reg_file_1 (
    .Read_Reg1(rs), .Read_Reg2(rt), .Reg_Write(RegWrite), .Write_Reg(multiplexer_1_out),
    .Write_Data(Write_data), .CLK(CLK), .Reset(Reset), .Read_Data1(reg_file_1_read_data1),
    .Read_Data2(reg_file_1_read_data2));
  Sign_Ext sign_ext_1 (.In16bit(imm), .Out32bit(sign_ext_1_out32bit));
  ALUControl alucontrol_1 (.ALUop(ALUop), .Funct(funct), .Op(alucontrol_1_op));
  Multiplexer #(.width(32)) multiplexer_2 (
    .in0(reg_file_1_read_data2), .in1(sign_ext_1_out32bit), .out(multiplexer_2_out), .sel(ALUSrc));
  Shift_left2 shift_left2_1 (.In32bit(sign_ext_1_out32bit), .Out32bit(shift_left2_1_out32bit));
  Adder #(.width(32)) adder_1 (.a(PCplus4), .b(shift_left2_1_out32bit), .out(adder_1_out));  // open: cin, cout
  ALU alu_1 (
    .In1(reg_file_1_read_data1), .In2(multiplexer_2_out), .ALU_Operation(alucontrol_1_op), .Zero(alu_1_zero),
    .Result(alu_1_result));
  and and_1 (and_1_out, Branch, alu_1_zero);
  Multiplexer #(.width(32)) multiplexer_3 (.in0(PCplus4), .in1(adder_1_out), .out(multiplexer_3_out), .sel(and_1_out));
  Data_memory data_memory_1 (
    .Address(alu_1_result), .MemWrite(MemWrite), .MemRead(MemRead), .CLK(CLK),
    .MemInput(reg_file_1_read_data2), .lhu(lhu), .MemOutput(data_memory_1_memoutput));
  Multiplexer #(.width(32)) multiplexer_4 (
    .in0(multiplexer_3_out), .in1(Jump_Address), .out(multiplexer_4_out), .sel(jal_control));
  Multiplexer #(.width(32)) multiplexer_5 (
    .in0(data_memory_1_memoutput), .in1(alu_1_result), .out(Write_data), .sel(MemtoReg));
  Multiplexer #(.width(32)) multiplexer_6 (
    .in0(multiplexer_4_out), .in1(reg_file_1_read_data1), .out(PCnext), .sel(jr_check));
endmodule

module Fetch (
  input  [31:0] PCnext,
  input  CLK,
  input  Reset,
  output [31:0] PC,
  output [31:0] PCplus4,
  output [31:0] Instruction
);

  wire [23:0] division_4_1_o;

  Register #(.width(32)) PCreg (.D(PCnext), .en(1'b1), .clk(CLK), .Q(PC), .clr(Reset));
  // Probe on PC
  Adder #(.width(32)) adder_1 (.a(PC), .b(32'h4), .out(PCplus4));  // open: cin, cout
  division_4 division_4_1 (.i(PC), .o(division_4_1_o));
  ROM #(.addrWidth(24), .dataWidth(32)) rom_1 (.addr(division_4_1_o), .data(Instruction));
  // Probe on PCplus4
  // Probe on division_4_1_o
  // Probe on Instruction

  // Notes on the sheet:
  //   contents of rom_1 (hex, n*v repeats v):
  //   112345 0 cab4
endmodule

module Ildown (
  input  [31:0] Instruction,
  output [25:0] address,
  output [15:0] imm,
  output [5:0] funct,
  output [4:0] shamt,
  output [4:0] rd,
  output [4:0] rt,
  output [4:0] rs,
  output [5:0] op
);


  assign address = Instruction[25:0];
  assign funct = Instruction[5:0];
  assign imm = Instruction[15:0];
  assign op = Instruction[31:26];
  assign rd = Instruction[15:11];
  assign rs = Instruction[25:21];
  assign rt = Instruction[20:16];
  assign shamt = Instruction[10:6];
endmodule

module Reg_File (
  input  [4:0] Read_Reg1,
  input  [4:0] Read_Reg2,
  input  Reg_Write,
  input  [4:0] Write_Reg,
  input  [31:0] Write_Data,
  input  CLK,
  input  Reset,
  output [31:0] Read_Data1,
  output [31:0] Read_Data2
);

  wire decoder_1_out0, decoder_1_out1, decoder_1_out2, decoder_1_out3, decoder_1_out4, decoder_1_out5,
       decoder_1_out6, decoder_1_out7, decoder_1_out8, decoder_1_out9, decoder_1_out10, decoder_1_out11,
       decoder_1_out12, decoder_1_out13, decoder_1_out14, decoder_1_out15, decoder_1_out16, decoder_1_out17,
       decoder_1_out18, decoder_1_out19, decoder_1_out20, decoder_1_out21, decoder_1_out22, decoder_1_out23,
       decoder_1_out24, decoder_1_out25, decoder_1_out26, decoder_1_out27, decoder_1_out28, decoder_1_out29,
       decoder_1_out30, decoder_1_out31;
  wire [31:0] a0, a1, a2, a3, at, fp, gp, k0, k1, ra, s0, s1, s2, s3, s4, s5, s6, s7, sp, t0, t1, t2, t3, t4,
       t5, t6, t7, t8, t9, v0, v1, zero;

  Decoder #(.select(5)) decoder_1 (
    .out0(decoder_1_out0), .out1(decoder_1_out1), .out2(decoder_1_out2), .out3(decoder_1_out3),
    .out4(decoder_1_out4), .out5(decoder_1_out5), .out6(decoder_1_out6), .out7(decoder_1_out7),
    .out8(decoder_1_out8), .out9(decoder_1_out9), .out10(decoder_1_out10), .out11(decoder_1_out11),
    .out12(decoder_1_out12), .out13(decoder_1_out13), .out14(decoder_1_out14), .out15(decoder_1_out15),
    .out16(decoder_1_out16), .out17(decoder_1_out17), .out18(decoder_1_out18), .out19(decoder_1_out19),
    .out20(decoder_1_out20), .out21(decoder_1_out21), .out22(decoder_1_out22), .out23(decoder_1_out23),
    .out24(decoder_1_out24), .out25(decoder_1_out25), .out26(decoder_1_out26), .out27(decoder_1_out27),
    .out28(decoder_1_out28), .out29(decoder_1_out29), .out30(decoder_1_out30), .out31(decoder_1_out31),
    .sel(Write_Reg), .en(Reg_Write));
  Register #(.width(32)) u_zero (.D({32{1'b0}}), .en(decoder_1_out0), .clk(CLK), .Q(zero), .clr(Reset));
  Register #(.width(32)) u_t0 (.D(Write_Data), .en(decoder_1_out8), .clk(CLK), .Q(t0), .clr(Reset));
  Register #(.width(32)) u_s0 (.D(Write_Data), .en(decoder_1_out16), .clk(CLK), .Q(s0), .clr(Reset));
  Register #(.width(32)) u_t8 (.D(Write_Data), .en(decoder_1_out24), .clk(CLK), .Q(t8), .clr(Reset));
  Register #(.width(32)) u_at (.D(Write_Data), .en(decoder_1_out1), .clk(CLK), .Q(at), .clr(Reset));
  Register #(.width(32)) u_t1 (.D(Write_Data), .en(decoder_1_out9), .clk(CLK), .Q(t1), .clr(Reset));
  Register #(.width(32)) u_s1 (.D(Write_Data), .en(decoder_1_out17), .clk(CLK), .Q(s1), .clr(Reset));
  Register #(.width(32)) u_t9 (.D(Write_Data), .en(decoder_1_out25), .clk(CLK), .Q(t9), .clr(Reset));
  Register #(.width(32)) u_v0 (.D(Write_Data), .en(decoder_1_out2), .clk(CLK), .Q(v0), .clr(Reset));
  Register #(.width(32)) u_t2 (.D(Write_Data), .en(decoder_1_out10), .clk(CLK), .Q(t2), .clr(Reset));
  Register #(.width(32)) u_s2 (.D(Write_Data), .en(decoder_1_out18), .clk(CLK), .Q(s2), .clr(Reset));
  Register #(.width(32)) u_k0 (.D(Write_Data), .en(decoder_1_out26), .clk(CLK), .Q(k0), .clr(Reset));
  Register #(.width(32)) u_v1 (.D(Write_Data), .en(decoder_1_out3), .clk(CLK), .Q(v1), .clr(Reset));
  Register #(.width(32)) u_t3 (.D(Write_Data), .en(decoder_1_out11), .clk(CLK), .Q(t3), .clr(Reset));
  Register #(.width(32)) u_s3 (.D(Write_Data), .en(decoder_1_out19), .clk(CLK), .Q(s3), .clr(Reset));
  Register #(.width(32)) u_k1 (.D(Write_Data), .en(decoder_1_out27), .clk(CLK), .Q(k1), .clr(Reset));
  Register #(.width(32)) u_a0 (.D(Write_Data), .en(decoder_1_out4), .clk(CLK), .Q(a0), .clr(Reset));
  Register #(.width(32)) u_t4 (.D(Write_Data), .en(decoder_1_out12), .clk(CLK), .Q(t4), .clr(Reset));
  Register #(.width(32)) u_s4 (.D(Write_Data), .en(decoder_1_out20), .clk(CLK), .Q(s4), .clr(Reset));
  Register #(.width(32)) u_gp (.D(Write_Data), .en(decoder_1_out28), .clk(CLK), .Q(gp), .clr(Reset));
  Register #(.width(32)) u_a1 (.D(Write_Data), .en(decoder_1_out5), .clk(CLK), .Q(a1), .clr(Reset));
  Register #(.width(32)) u_t5 (.D(Write_Data), .en(decoder_1_out13), .clk(CLK), .Q(t5), .clr(Reset));
  Register #(.width(32)) u_s5 (.D(Write_Data), .en(decoder_1_out21), .clk(CLK), .Q(s5), .clr(Reset));
  Register #(.width(32)) u_sp (.D(Write_Data), .en(decoder_1_out29), .clk(CLK), .Q(sp), .clr(Reset));
  Register #(.width(32)) u_a2 (.D(Write_Data), .en(decoder_1_out6), .clk(CLK), .Q(a2), .clr(Reset));
  Register #(.width(32)) u_t6 (.D(Write_Data), .en(decoder_1_out14), .clk(CLK), .Q(t6), .clr(Reset));
  Register #(.width(32)) u_s6 (.D(Write_Data), .en(decoder_1_out22), .clk(CLK), .Q(s6), .clr(Reset));
  Register #(.width(32)) u_fp (.D(Write_Data), .en(decoder_1_out30), .clk(CLK), .Q(fp), .clr(Reset));
  Multiplexer #(.select(5), .width(32)) multiplexer_1 (
    .in0(zero), .in1(at), .in2(v0), .in3(v1), .in4(a0), .in5(a1), .in6(a2), .in7(a3), .in8(t0), .in9(t1),
    .in10(t2), .in11(t3), .in12(t4), .in13(t5), .in14(t6), .in15(t7), .in16(s0), .in17(s1), .in18(s2),
    .in19(s3), .in20(s4), .in21(s5), .in22(s6), .in23(s7), .in24(t8), .in25(t9), .in26(k0), .in27(k1),
    .in28(gp), .in29(sp), .in30(fp), .in31(ra), .out(Read_Data1), .sel(Read_Reg1));
  Multiplexer #(.select(5), .width(32)) multiplexer_2 (
    .in0(zero), .in1(at), .in2(v0), .in3(v1), .in4(a0), .in5(a1), .in6(a2), .in7(a3), .in8(t0), .in9(t1),
    .in10(t2), .in11(t3), .in12(t4), .in13(t5), .in14(t6), .in15(t7), .in16(s0), .in17(s1), .in18(s2),
    .in19(s3), .in20(s4), .in21(s5), .in22(s6), .in23(s7), .in24(t8), .in25(t9), .in26(k0), .in27(k1),
    .in28(gp), .in29(sp), .in30(fp), .in31(ra), .out(Read_Data2), .sel(Read_Reg2));
  Register #(.width(32)) u_a3 (.D(Write_Data), .en(decoder_1_out7), .clk(CLK), .Q(a3), .clr(Reset));
  Register #(.width(32)) u_t7 (.D(Write_Data), .en(decoder_1_out15), .clk(CLK), .Q(t7), .clr(Reset));
  Register #(.width(32)) u_s7 (.D(Write_Data), .en(decoder_1_out23), .clk(CLK), .Q(s7), .clr(Reset));
  Register #(.width(32)) u_ra (.D(Write_Data), .en(decoder_1_out31), .clk(CLK), .Q(ra), .clr(Reset));
endmodule

module ALU (
  input  [31:0] In1,
  input  [31:0] In2,
  input  [2:0] ALU_Operation,
  output Zero,
  output [31:0] Result
);

  wire Comp;
  wire [31:0] ADD, And_logic, Nor_logic, Or_logic, SUB;

  Adder #(.width(32)) adder_1 (.a(In1), .b(In2), .out(ADD));  // open: cin, cout
  Subtractor #(.width(32)) subtractor_1 (.a(In1), .b(In2), .out(SUB));  // open: bin, bout
  Comparator #(.width(32)) comparator_1 (.a(In1), .b(In2), .lt(Comp));  // open: gt, eq
  assign And_logic = In1 & In2;  // AND_Gate and_1, 32 bits wide
  assign Nor_logic = ~(In1 | In2);  // NOR_Gate nor_1, 32 bits wide
  assign Or_logic = In1 | In2;  // OR_Gate or_1, 32 bits wide
  Multiplexer #(.select(3), .width(32)) multiplexer_1 (
    .in0(And_logic), .in1(Or_logic), .in2(ADD), .in3(SUB), .in4({{31{1'b0}}, Comp}), .in5(Nor_logic),
    .out(Result), .sel(ALU_Operation));  // open: in6, in7
  Comparator #(.width(32)) comparator_2 (.a(Result), .b({32{1'b0}}), .eq(Zero));  // open: gt, lt

  // Other names for the same wires on the sheet: SLT[0] = Comp
endmodule

module Sign_Ext (
  input  [15:0] In16bit,
  output [31:0] Out32bit
);


  assign Out32bit = {{17{In16bit[15]}}, In16bit[14:0]};
endmodule

module Shift_left2 (
  input  [31:0] In32bit,
  output [31:0] Out32bit
);

  // Probe on In32bit
  // Probe on {In32bit[29:0], 2'b00}

  assign Out32bit = {In32bit[29:0], 2'b00};
endmodule

module Data_memory (
  input  [31:0] Address,
  input  MemWrite,
  input  MemRead,
  input  CLK,
  input  [31:0] MemInput,
  input  lhu,
  output [31:0] MemOutput
);

  wire [15:0] multiplexer_2_out;
  wire [31:0] bit_extender_1_out, ram_1_dout;

  RAM #(.addrWidth(24), .asyncread("true"), .dataWidth(32)) ram_1 (
    .addr(Address[25:2]), .we(MemWrite), .oe(MemRead), .clk(CLK), .din(MemInput), .dout(ram_1_dout));
  // Probe on Address[1:0]
  // Probe on ram_1_dout
  Multiplexer #(.width(32)) multiplexer_1 (.in0(ram_1_dout), .in1(bit_extender_1_out), .out(MemOutput), .sel(lhu));
  Multiplexer #(.select(2), .width(16)) multiplexer_2 (
    .in0(ram_1_dout[15:0]), .in1(ram_1_dout[15:0]), .in2(ram_1_dout[31:16]), .in3(ram_1_dout[31:16]),
    .out(multiplexer_2_out), .sel(Address[1:0]));
  assign bit_extender_1_out = {{16{1'b0}}, multiplexer_2_out};  // Bit_Extender bit_extender_1
  // Probe on bit_extender_1_out

  // Other names for the same wires on the sheet: LineSelect1[1:0] = Address[1:0]
endmodule

module division_4 (
  input  [31:0] i,
  output [23:0] o
);


  assign o = i[25:2];
endmodule

module control_v1 (
  input  [5:0] OP,
  output RegDst,
  output ALUSrc,
  output MemtoReg,
  output RegWrite,
  output MemRead,
  output MemWrite,
  output Branch,
  output [1:0] ALUop,
  output Jump,
  output Link
);

  wire and_3_out, and_4_out, not_1_out, not_2_out, not_3_out, not_4_out, not_5_out, not_6_out, not_7_out,
       not_8_out, not_9_out, not_10_out, not_11_out, not_12_out;

  not not_1 (not_1_out, OP[3]);
  not not_2 (not_2_out, OP[1]);
  or or_1 (ALUSrc, OP[1], OP[3]);
  not not_3 (not_3_out, OP[3]);
  not not_4 (not_4_out, OP[2]);
  not not_5 (not_5_out, OP[1]);
  not not_6 (not_6_out, OP[3]);
  not not_7 (not_7_out, OP[3]);
  not not_8 (not_8_out, OP[3]);
  not not_9 (not_9_out, OP[2]);
  not not_10 (not_10_out, OP[1]);
  not not_11 (not_11_out, OP[5]);
  not not_12 (not_12_out, OP[5]);
  and and_1 (RegDst, not_1_out, not_2_out);
  and and_2 (MemtoReg, not_3_out, OP[1]);
  and and_3 (and_3_out, not_4_out, not_5_out);
  and and_4 (and_4_out, not_6_out, OP[0]);
  and and_5 (MemRead, OP[5], not_7_out);
  and and_6 (MemWrite, OP[5], OP[3]);
  and and_7 (ALUop[1], not_8_out, not_9_out, not_10_out);
  and and_8 (Jump, not_11_out, OP[1]);
  and and_9 (Link, not_12_out, OP[0]);
  or or_2 (RegWrite, and_3_out, and_4_out);

  assign ALUop[0] = OP[2];
  assign Branch = OP[2];

  // Other names for the same wires on the sheet: alupo[1:0] = {ALUop[1], OP[2]}
endmodule

module ALUControl (
  input  [1:0] ALUop,
  input  [5:0] Funct,
  output [2:0] Op
);

  wire and_1_out, and_2_out, and_3_out, not_2_out, not_3_out, not_4_out, not_5_out;
  wire [2:0] or_2_out;
  wire [2:2] not_1_out;

  not not_1 (not_1_out[2], ALUop[0]);
  not not_2 (not_2_out, Funct[2]);
  not not_3 (not_3_out, Funct[1]);
  not not_4 (not_4_out, Funct[3]);
  not not_5 (not_5_out, Funct[2]);
  and and_1 (and_1_out, not_2_out, not_3_out);
  and and_2 (and_2_out, Funct[2], Funct[1]);
  and and_3 (and_3_out, not_4_out, not_5_out);
  or or_1 (or_2_out[2], and_1_out, and_2_out, Funct[3]);
  or or_2 (or_2_out[0], and_3_out, Funct[0]);
  Multiplexer #(.width(3)) multiplexer_1 (
    .in0({not_1_out[2], 2'b01}), .in1({or_2_out[2], Funct[2], or_2_out[0]}), .out(Op), .sel(ALUop[1]));

  // Other names for the same wires on the sheet: F = ALUop[1]
endmodule

module instructrion15_0 (
  input  [31:0] i,
  output [5:0] intruc_5_0
);


  assign intruc_5_0 = i[5:0];
endmodule

module control_v2 (
  input  [5:0] Op,
  output RegDst,
  output ALUSrc,
  output MemtoReg,
  output RegWrite,
  output MemRead,
  output MemWrite,
  output Branch,
  output [1:0] ALUOp,
  output lhu,
  output andi,
  output jal
);

  wire and_2_out, and_3_out, and_4_out, and_7_out, and_8_out, and_9_out, and_10_out, and_11_out, not_1_out,
       not_2_out, not_3_out, not_4_out, not_5_out;

  not not_1 (not_1_out, Op[5]);
  not not_2 (not_2_out, Op[3]);
  not not_3 (not_3_out, Op[2]);
  not not_4 (not_4_out, Op[1]);
  not not_5 (not_5_out, Op[0]);
  and and_1 (RegDst, not_1_out, not_2_out);
  or or_1 (ALUSrc, Op[0], Op[3]);
  and and_2 (and_2_out, not_2_out, not_3_out);
  and and_3 (and_3_out, Op[3], Op[2]);
  and and_4 (and_4_out, Op[5], not_2_out);
  and and_5 (MemRead, not_2_out, Op[0]);
  and and_6 (MemWrite, Op[3], not_3_out);
  and and_7 (and_7_out, not_1_out, Op[1]);
  and and_8 (and_8_out, not_2_out, Op[2], not_5_out);
  and and_9 (and_9_out, not_1_out, Op[3], not_3_out);
  and and_10 (and_10_out, not_1_out, Op[1]);
  and and_11 (and_11_out, not_2_out, Op[2], not_5_out);
  and and_12 (ALUOp[0], not_2_out, not_3_out, not_4_out);
  and and_13 (lhu, Op[5], not_4_out);
  and and_14 (andi, Op[3], Op[2]);
  and and_15 (jal, not_1_out, Op[1]);
  or or_2 (RegWrite, and_2_out, and_3_out, and_4_out);
  or or_3 (Branch, and_7_out, and_8_out, and_9_out);
  or or_4 (ALUOp[1], and_10_out, and_11_out);

  assign MemtoReg = Op[0];
endmodule

module jal (
  input  [25:0] Instruction,
  input  [31:0] PCplus4,
  output [31:0] Jump_Address
);

  // Probe on nothing
  assign Jump_Address[27:0] = {{2{1'b0}}, {Instruction[23:0], 2'b00}};  // Bit_Extender bit_extender_1
  // Probe on {PCplus4[31:28], Jump_Address[27:0]}

  assign Jump_Address[31:28] = PCplus4[31:28];
endmodule

module jr (
  input  [5:0] Op,
  input  [1:0] ALUop,
  output jr_check
);

  wire and_1_out, and_2_out;

  and and_1 (and_1_out, ~Op[0], ~Op[1], ~Op[2], ~Op[4], ~Op[5], Op[3]);  // AND_Gate
  and and_2 (and_2_out, ALUop[1], ~ALUop[0]);  // AND_Gate
  and and_3 (jr_check, and_2_out, and_1_out);
endmodule

module andi (
  input  rs,
  input  rt,
  input  [15:0] inm
);

  Bit_Extender #(.in_width(16), .out_width(32), .\type ("zero")) bit_extender_1 (.in(inm));  // open: out
endmodule
